# Fritzing sketch load_cell_schematic (saved by Fritzing 0.9.3b)
breadboards: 1

parts:
  HX711 = HX711 Weighing Sensor Module
  Componente3 = LCD1602-I2C
  Componente4 = Arduino Nano (Rev3.0)
  Load_Cell2 = Load Cell - Red/white/black/green
  Sensor1 = TTP223B Capacitive Touch Sensor Module

nets:
  N1: HX711.VCC, Componente4.D10
  GND: HX711.GND, Componente3.GND, Componente4.GND, Sensor1.GND
  VCC: HX711.DO/RX, Componente3.VCC, Componente4.5V, Sensor1.VCC
  N2: HX711.CK/TX, Componente4.D9
  N3: HX711.E+, Load_Cell2.wire1
  N4: HX711.E-, Load_Cell2.wire3
  N5: HX711.A+, Load_Cell2.wire2
  N6: HX711.A-, Load_Cell2.wire4
  N7: Componente3.SDA, Componente4.A4
  N8: Componente3.SCL, Componente4.A5
  N9: Componente4.D3, Sensor1.SIG

custom parts:
  HX711 Weighing Sensor Module: HX711 is a precision 24-bit analog-to-digital converter (ADC) designed for weigh scales and industrial control applications to interface directly with a bridge sensor.
  LCD1602-I2C: A standard character display, usually with 2x16 characters. Comes in many colors with LCM1602 IIC attached.
  Load Cell - Red/white/black/green: A rectangle load cell/weighting pressure Sensor with four wires - Red, white, black, green. Normally corresponding with E+, E-, A+, A- respectively.
  TTP223B Capacitive Touch Sensor Module: The TTP223B capacitive touch sensor module uses the TTP223B IC. The appropriate voltage is approximately 2 to 5.5 volts.
